# Fritzing sketch Project 2 Fritzing (saved by Fritzing 0.9.3b)
breadboards: 2

parts:
  J1 = Basic Servo
  J2 = Basic Servo
  J3 = Basic Servo
  Raspberry_Pi_1 = Raspberry Pi 3 [part_number=RPI-3-V1.2]
  J4 = T Cobbler Plus
  hc-sr1 = hc-sr04
  R1 = Resistor [tolerance=±5% resistance=330 package=THT]
  R2 = Resistor [tolerance=±5% resistance=330 package=THT]
  R3 = Resistor [tolerance=±5% resistance=330 package=THT]
  R4 = Resistor [tolerance=±5% resistance=220 package=THT]
  R5 = Resistor [tolerance=±5% resistance=220 package=THT]
  LED4 = RGB LED (com. anode, rbg) [package="5 mm [THT]"]
  CAMERA1 = TTL Serial JPEG Camera  # not connected
  LCD1 = LCD screen
  U1 = POT [package=pot_mammoth]
  R6 = Resistor [tolerance=±5% resistance=220 package="2010 [SMD]"]

nets:
  VCC: J1.vcc, J2.vcc, J3.vcc, hc-sr1.VCC
  GND: J2.gnd, J3.gnd, hc-sr1.GND, R4.Pin_1, LED4.common_anode
  3V3: Raspberry_Pi_1.3v3, Raspberry_Pi_1.3V3, J4.3.3V
  N1: Raspberry_Pi_1.GPIO2, J4.GPIO_2
  N2: Raspberry_Pi_1.GPIO3, J4.GPIO_3
  N3: Raspberry_Pi_1.GIPO4, J4.GPIO_4
  GND_2: Raspberry_Pi_1.GND, J4.GND
  N4: Raspberry_Pi_1.GIPO17, J4.GPIO_17
  N5: Raspberry_Pi_1.GIPO27, J4.GPIO_27
  N6: Raspberry_Pi_1.GIPO22, J4.GPIO_22
  N7: Raspberry_Pi_1.GIPO10, J4.GPIO_10
  N8: Raspberry_Pi_1.GIPO9, J4.GPIO_9
  N9: Raspberry_Pi_1.GIPO11, J4.GPIO_11
  N10: Raspberry_Pi_1.ID_SD, J4.ID_SD
  N11: Raspberry_Pi_1.GIPO5, J4.GPIO_5
  N12: Raspberry_Pi_1.GIPO6, J4.GPIO_6
  N13: Raspberry_Pi_1.GIPO13, J4.GPIO_13
  N14: Raspberry_Pi_1.GIPO19, J4.GPIO_19
  N15: Raspberry_Pi_1.GIPO26, J4.GPIO_26
  N16: Raspberry_Pi_1.GIPO21, J4.GPIO_21
  N17: Raspberry_Pi_1.GIPO20, J4.GPIO_20
  N18: Raspberry_Pi_1.GIPO16, J4.GPIO_16
  N19: Raspberry_Pi_1.GIPO12, J4.GPIO_12
  N20: Raspberry_Pi_1.ID_SC, J4.ID_SC
  N21: Raspberry_Pi_1.GIPO7, J4.GPIO_7
  N22: Raspberry_Pi_1.GIPO8, J4.GPIO_8
  N23: Raspberry_Pi_1.GIPO25, J4.GPIO_25
  N24: Raspberry_Pi_1.GIPO24, J4.GPIO_24
  N25: Raspberry_Pi_1.GIPO23, J4.GPIO_23
  N26: Raspberry_Pi_1.GIPO18, J4.GPIO_18
  N27: Raspberry_Pi_1.GIPO15, J4.GPIO_15
  N28: Raspberry_Pi_1.GIPO14, J4.GPIO_14
  5V: Raspberry_Pi_1.5V, J4.5V
  N29: hc-sr1.Echo, R5.Pin_0
  N30: R1.Pin_1, LED4.blue_cathode
  N31: R2.Pin_1, LED4.green_cathode
  N32: R3.Pin_1, LED4.red_cathode
  N33: R4.Pin_0, R5.Pin_1
  N34: LCD1.VSS, LCD1.R/W, LCD1.LED-, U1.E
  N35: LCD1.VDD, U1.S, R6.Pin_1
  N36: LCD1.V0, U1.A
  N37: LCD1.LED+, R6.Pin_0

custom parts:
  T Cobbler Plus: The T-Cobbler Plus is an add on prototyping board from Adafruit specifically designed for the Raspberry Pi B+ that can break out all those tasty power, GPIO, I2C and SPI pins from the 40-pin header onto a solderless breadboard. This set will make "cobbling together" prototypes with the Pi super easy. The T-Cobbler Plus can plug into any solderless breadboard.
  TTL Serial JPEG Camera: TTL Serial JPEG Camera with NTSC Out
